# Fritzing sketch basicbot (saved by Fritzing 0.8.7b)
breadboards: 1

parts:
  Motor_Shield1 = Arduino Motor Shield (Rev3)
  Motor_A1 = DC Motor
  Motor_B1 = DC Motor
  BATT1 = 4xAA Switchable Battery Pack w/Bare Wire
  Ping_Sensor2 = SRF05 Ultrasonic Rangefinder

nets:
  N1: Motor_Shield1.D4, Ping_Sensor2.Echo
  N2: Motor_Shield1.D7, Ping_Sensor2.Trig
  N3: Motor_Shield1.B-, Motor_A1.pin_2
  N4: Motor_Shield1.B+, Motor_A1.pin_1
  N5: Motor_Shield1.A-, Motor_B1.pin_2
  N6: Motor_Shield1.A+, Motor_B1.pin_1
  N7: Motor_Shield1.VMOT, BATT1.POS
  GND: Motor_Shield1.GND, BATT1.NEG, Ping_Sensor2.GND
  5V: Motor_Shield1.5V, Ping_Sensor2.VCC

notes:
  Cut the "Vin Connect" on the back of the motor shield so the power to the motors is separate from the Arduino's

custom parts:
  4xAA Switchable Battery Pack w/Bare Wire: 4xAA Switchable Battery Pack with Bare Wire connection
