# Fritzing sketch battery (saved by Fritzing 0.8.7b)
breadboards: 1

parts:
  Part1 = Arduino Uno (Rev3)
  Red_LED = LED - 5mm [color="Red (633nm)" package="5 mm [THT]"]
  Resistor5 = Resistor [tolerance=±5% resistance=220 package=THT]
  Resistor4 = Resistor [tolerance=±5% resistance=220 package=THT]
  Resistor3 = Resistor [tolerance=±5% resistance=220 package=THT]
  Green_LED = LED - 5mm [color="Green (560nm)" package="5 mm [THT]"]
  Yellow_LED = LED - 5mm [color="Yellow (585nm)" package="5 mm [THT]"]

nets:
  N1: Part1.A2, Resistor3.Pin_1
  N2: Part1.D8, Resistor4.Pin_1
  N3: Part1.D9_PWM, Resistor5.Pin_1
  N4: Part1.GND, Red_LED.cathode, Green_LED.cathode, Yellow_LED.cathode
  N5: Red_LED.anode, Resistor3.Pin_0
  N6: Resistor5.Pin_0, Green_LED.anode
  N7: Resistor4.Pin_0, Yellow_LED.anode
