# Fritzing sketch battery_indicator (saved by Fritzing 0.8.7b)
breadboards: 1

parts:
  Part1 = Arduino Uno (Rev3)
  Resistor1 = Resistor [tolerance=±5% resistance=220 package=THT]
  Resistor3 = Resistor [tolerance=±5% resistance=220 package=THT]
  Resistor5 = Resistor [tolerance=±5% resistance=220 package=THT]
  LED2 = LED - 5mm [color="Red (633nm)" package="5 mm [THT]"]
  LED4 = LED - 5mm [color="Green (560nm)" package="5 mm [THT]"]
  LED6 = LED - 5mm [color="Yellow (585nm)" package="5 mm [THT]"]

nets:
  N1: Part1.A5/SCL, Resistor1.Pin_1
  N2: Part1.D8, Resistor5.Pin_1
  N3: Part1.D9_PWM, Resistor3.Pin_1
  N4: Part1.GND, LED2.cathode, LED4.cathode, LED6.cathode
  N5: Resistor1.Pin_0, LED2.anode
  N6: Resistor3.Pin_0, LED4.anode
  N7: Resistor5.Pin_0, LED6.anode

notes:
  We will be cutting the "BRAKE DISABLE" on the motor shield to free up pins 8 & 9.
