# Fritzing sketch breadboard_arduino (saved by Fritzing 0.8.7b)
breadboards: 1

parts:
  LED = LED - 5mm [color="Red (633nm)" package="5 mm [THT]"]
  Resistor = Resistor [tolerance=±5% resistance=220 package=THT]
  U1 = atmega328 [package=dip]
  Resistor1 = Resistor [tolerance=±5% resistance=10k package=THT]
  C1 = Ceramic Capacitor [capacitance=100nF package="100 mil [THT, multilayer]"]

nets:
  N1: LED.cathode, Resistor.Pin_1
  N2: LED.anode, U1.D13
  N3: Resistor.Pin_0, U1.GND#21
  N4: U1.RESET, Resistor1.Pin_0, C1.1
  N5: U1.VCC, Resistor1.Pin_1

notes:
  http://shrimping.it/blog/blink/
