# Fritzing sketch button (saved by Fritzing 0.8.7b)
breadboards: 1

parts:
  Part1 = Arduino Uno (Rev3)
  LED = LED - 5mm [color="Red (633nm)" package="5 mm [THT]"]
  Switch = Pushbutton [package="[THT]"]
  Resistor = Resistor [tolerance=±5% resistance=220 package=THT]
  Resistor_2 = Resistor [tolerance=±5% resistance=10k package=THT]
  R1 = Resistor [tolerance=±5% resistance=220 package=THT]

nets (from the breadboard view):
  N1: Part1.D13/SCK, Resistor.Pin_0
  N2: Part1.GND, LED.cathode, Resistor_2.Pin_0
  N3: Part1.D2, R1.Pin_1
  N4: Part1.5V, Switch.Pin_3, Switch.Pin_4
  N5: LED.anode, Resistor.Pin_1
  N6: Switch.Pin_1, Switch.Pin_2, Resistor_2.Pin_1, R1.Pin_0

notes:
  Examples -> 02. Digital -> Button
  http://www.arduino.cc/en/Tutorial/Button
