# Fritzing sketch buzzer (saved by Fritzing 0.8.7b)
breadboards: 1

parts:
  Part1 = Arduino Uno (Rev3)
  LED1 = LED - 5mm [color="Red (633nm)" package="5 mm [THT]"]
  R2 = Resistor [tolerance=±5% resistance=220 package=THT]
  R1 = Resistor [tolerance=±5% resistance=220 package=THT]
  Buzzer = Piezo Speaker

nets:
  N1: Part1.D13/SCK, R1.Pin_0
  N2: Part1.GND, LED1.cathode, Buzzer.pin1
  N3: Part1.D2, R2.Pin_0
  N4: LED1.anode, R1.Pin_1
  N5: R2.Pin_1, Buzzer.pin2

notes:
  http://arduino.cc/en/Tutorial/Tone
