# Fritzing sketch ir_remote_part_2 (saved by Fritzing 0.8.7b)
breadboards: 1

parts:
  Part1 = Arduino Uno (Rev3)
  LED = LED - 5mm [color="Red (633nm)" package="5 mm [THT]"]
  Resistor = Resistor [tolerance=±5% resistance=220 package=THT]
  IR_Sensor = mystery part, 3 pins [chip_label="IR Receiver"]

nets:
  N1: Part1.D12/MISO, IR_Sensor.pin1
  N2: Part1.D13/SCK, Resistor.Pin_1
  N3: Part1.GND, LED.cathode, IR_Sensor.pin2
  N4: Part1.5V, IR_Sensor.pin3
  N5: LED.anode, Resistor.Pin_0

notes:
  http://arduino-info.wikispaces.com/IR-RemoteControl
  https://learn.adafruit.com/ir-sensor/testing-an-ir-sensor
