# Fritzing sketch magbot (saved by Fritzing 0.9.0b)
breadboards: 1

parts:
  Motor_Shield = Arduino Motor Shield (Rev3)
  Motor_A = DC Motor
  Motor_B = DC Motor
  Ping_Sensor = SRF05 Ultrasonic Rangefinder
  Buzzer = Piezo Speaker
  R2 = Resistor [tolerance=±5% resistance=220 package=THT]
  R4 = Resistor [tolerance=±5% resistance=220 package=THT]
  R5 = Resistor [tolerance=±5% resistance=220 package=THT]
  Part1 = Thumb Joystick
  BATT2 = 4xAA Switchable Battery Pack w/Bare Wire
  IR_Sensor2 = mystery part, 3 pins [chip_label="IR Receiver"]
  R6 = Resistor [tolerance=±5% resistance=220 package=THT]
  R7 = Resistor [tolerance=±5% resistance=220 package=THT]
  R8 = Resistor [tolerance=±5% resistance=220 package=THT]
  LED3 = LED - 5mm [color="Red (633nm)" package="5 mm [THT]"]
  LED7 = LED - 5mm [color="Yellow (585nm)" package="5 mm [THT]"]
  LED8 = LED - 5mm [color="Green (560nm)" package="5 mm [THT]"]

nets (from the breadboard view):
  N1: Motor_Shield.A0, R6.Pin_0
  N2: Motor_Shield.A1, R7.Pin_0
  N3: Motor_Shield.A2, R8.Pin_0
  N4: Motor_Shield.A4, Part1.HORZ
  N5: Motor_Shield.A5, Part1.VERT
  N6: Motor_Shield.D10_PWM, IR_Sensor2.pin1
  N7: Motor_Shield.D11_PWM/B, R5.Pin_0
  GND: Motor_Shield.GND, Ping_Sensor.GND, Buzzer.pin1, Part1.GND, BATT2.NEG, IR_Sensor2.pin2, LED3.cathode, LED7.cathode, LED8.cathode
  N8: Motor_Shield.D2, R2.Pin_0
  N9: Motor_Shield.D3_PWM/A, R4.Pin_1
  N10: Motor_Shield.D4, Ping_Sensor.Echo
  N11: Motor_Shield.D5_PWM, R4.Pin_0
  N12: Motor_Shield.D6_PWM, R5.Pin_1
  N13: Motor_Shield.D7, Ping_Sensor.Trig
  N14: Motor_Shield.B-, Motor_A.pin_2
  N15: Motor_Shield.B+, Motor_A.pin_1
  N16: Motor_Shield.A-, Motor_B.pin_2
  N17: Motor_Shield.A+, Motor_B.pin_1
  N18: Motor_Shield.VMOT, BATT2.POS
  VCC: Motor_Shield.5V, Ping_Sensor.VCC, Part1.VCC, IR_Sensor2.pin3
  N19: Buzzer.pin2, R2.Pin_1
  N20: R6.Pin_1, LED3.anode
  N21: R7.Pin_1, LED7.anode
  N22: R8.Pin_1, LED8.anode

notes:
  Cut the "Vin Connect" on the back of the motor shield so the power to the motors is separate from the Arduino's
  Cut SNS1 & SNS0 on the back of the motor shield so we can use pins A0 & A1s

custom parts:
  4xAA Switchable Battery Pack w/Bare Wire: 4xAA Switchable Battery Pack with Bare Wire connection
