# Fritzing sketch magbot_budget (saved by Fritzing 0.9.0b)
breadboards: 1

parts:
  Part1 = Arduino Nano (Rev3.0)
  IC1 = L293D [package=THT]
  BATT2 = 4xAA Switchable Battery Pack w/Bare Wire
  Motor_A2 = DC Motor
  Motor_B2 = DC Motor
  Ping_Sensor3 = SRF05 Ultrasonic Rangefinder
  Buzzer1 = Piezo Speaker
  R3 = Resistor [tolerance=±5% resistance=220 package=THT]
  IR_Sensor1 = mystery part, 3 pins [chip_label="IR Receiver"]

nets:
  GND: Part1.GND, IC1.0V, BATT2.NEG, Ping_Sensor3.GND, Buzzer1.pin1, IR_Sensor1.pin2
  N1: Part1.D2, R3.Pin_1
  N2: Part1.D4, Ping_Sensor3.Echo
  N3: Part1.D5, IC1.Enable_1
  N4: Part1.D6, IC1.Enable_2
  N5: Part1.D7, Ping_Sensor3.Trig
  N6: Part1.D8, IC1.In_1
  N7: Part1.D10, IR_Sensor1.pin1
  N8: Part1.D12/MISO, IC1.In_2
  5V: Part1.5V, IC1.+V, Ping_Sensor3.VCC
  N9: Part1.A5, IC1.In_4
  N10: Part1.A4, IC1.In_3
  N11: IC1.Out_1_(_Controlled_by_Enable_1_), Motor_B2.pin_2
  N12: IC1.Out_2_(_Controlled_by_Enable_1_), Motor_B2.pin_1
  N13: IC1.+Vmotor, BATT2.POS, IR_Sensor1.pin3
  N14: IC1.Out_3_(_Controlled_by_Enable_2_), Motor_A2.pin_2
  N15: IC1.Out_4_(_Controlled_by_Enable_2_), Motor_A2.pin_1
  N16: Buzzer1.pin2, R3.Pin_0

custom parts:
  4xAA Switchable Battery Pack w/Bare Wire: 4xAA Switchable Battery Pack with Bare Wire connection
