# Fritzing sketch matrix (saved by Fritzing 0.8.7b)
breadboards: 1

parts:
  Part1 = Arduino Uno (Rev3)
  Resistor8 = Resistor [tolerance=±5% resistance=220 package=THT]
  Resistor9 = Resistor [tolerance=±5% resistance=220 package=THT]
  Resistor10 = Resistor [tolerance=±5% resistance=220 package=THT]
  Resistor11 = Resistor [tolerance=±5% resistance=220 package=THT]
  Resistor12 = Resistor [tolerance=±5% resistance=220 package=THT]
  Resistor13 = Resistor [tolerance=±5% resistance=220 package=THT]
  Resistor14 = Resistor [tolerance=±5% resistance=220 package=THT]
  Resistor15 = Resistor [tolerance=±5% resistance=220 package=THT]
  8x8_LED_Matrix2 = 8x8 LED Matrix

nets:
  N1: Part1.A0, 8x8_LED_Matrix2.Pin_8
  N2: Part1.A1, 8x8_LED_Matrix2.Pin_7
  N3: Part1.A2, Resistor13.Pin_0
  N4: Part1.A3, 8x8_LED_Matrix2.Pin_5
  N5: Part1.D8, Resistor8.Pin_0
  N6: Part1.D9_PWM, 8x8_LED_Matrix2.Pin_9
  N7: Part1.D10_PWM/SS, 8x8_LED_Matrix2.Pin_1
  N8: Part1.D11_PWM/MOSI, 8x8_LED_Matrix2.Pin_2
  N9: Part1.D12/MISO, Resistor10.Pin_0
  N10: Part1.D13/SCK, Resistor9.Pin_0
  N11: Part1.D2, Resistor15.Pin_0
  N12: Part1.D3_PWM, Resistor14.Pin_0
  N13: Part1.D4, 8x8_LED_Matrix2.Pin14
  N14: Part1.D5_PWM, Resistor11.Pin_0
  N15: Part1.D6_PWM, 8x8_LED_Matrix2.Pin_12
  N16: Part1.D7, Resistor12.Pin_0
  N17: Resistor8.Pin_1, 8x8_LED_Matrix2.Pin_10
  N18: Resistor9.Pin_1, 8x8_LED_Matrix2.Pin_4
  N19: Resistor10.Pin_1, 8x8_LED_Matrix2.Pin_3
  N20: Resistor11.Pin_1, 8x8_LED_Matrix2.Pin_13
  N21: Resistor12.Pin_1, 8x8_LED_Matrix2.Pin_11
  N22: Resistor13.Pin_1, 8x8_LED_Matrix2.Pin_6
  N23: Resistor14.Pin_1, 8x8_LED_Matrix2.Pin_15
  N24: Resistor15.Pin_1, 8x8_LED_Matrix2.Pin_16

custom parts:
  8x8 LED Matrix: Red Color Common Anode 8x8 LED Matrix
