# Fritzing sketch midi (saved by Fritzing 0.8.7b)

parts:
  Part1 = Arduino Uno (Rev3)
  R1 = Resistor [tolerance=±5% resistance=220 package=THT]
  DIN1 = DIN-5 jack (MIDI) [package=THT]

nets:
  GND: Part1.GND, DIN1.GND
  N1: Part1.D1/TX, DIN1.5
  N2: Part1.5V, R1.Pin_1
  N3: R1.Pin_0, DIN1.4

notes:
  http://arduino.cc/en/Tutorial/midi
