# Fritzing sketch motors (saved by Fritzing 0.8.7b)

parts:
  Motor_Shield1 = Arduino Motor Shield (Rev3)
  Motor_A1 = DC Motor
  Motor_B1 = DC Motor
  BATT1 = 4xAA Switchable Battery Pack w/Bare Wire

nets:
  N1: Motor_Shield1.B-, Motor_A1.pin_2
  N2: Motor_Shield1.B+, Motor_A1.pin_1
  N3: Motor_Shield1.A-, Motor_B1.pin_2
  N4: Motor_Shield1.A+, Motor_B1.pin_1
  N5: Motor_Shield1.VMOT, BATT1.POS
  N6: Motor_Shield1.GND, BATT1.NEG

notes:
  Cut the "Vin Connect" on the back of the motor shield so the power to the motors is separate from the Arduino's

custom parts:
  4xAA Switchable Battery Pack w/Bare Wire: 4xAA Switchable Battery Pack with Bare Wire connection
