# Fritzing sketch ping (saved by Fritzing 0.8.7b)
breadboards: 1

parts:
  Part1 = Arduino Uno (Rev3)
  LED = LED - 5mm [color="Red (633nm)" package="5 mm [THT]"]
  Resistor = Resistor [tolerance=±5% resistance=220 package=THT]
  Ping_Sensor1 = SRF05 Ultrasonic Rangefinder

nets:
  N1: Part1.D11_PWM/MOSI, Ping_Sensor1.Echo
  N2: Part1.D12/MISO, Ping_Sensor1.Trig
  N3: Part1.D13/SCK, Resistor.Pin_1
  GND: Part1.GND, LED.cathode, Ping_Sensor1.GND
  5V: Part1.5V, Ping_Sensor1.VCC
  N4: LED.anode, Resistor.Pin_0

notes:
  http://playground.arduino.cc/Code/NewPing
