# Fritzing sketch servo (saved by Fritzing 0.8.7b)

parts:
  Part1 = Arduino Uno (Rev3)
  J1 = Basic Servo

nets:
  N1: Part1.D9_PWM, J1.pulse
  GND: Part1.GND, J1.gnd
  5V: Part1.5V, J1.vcc

notes:
  http://arduino.cc/en/Tutorial/sweep
