# Fritzing sketch servo_thumbstick (saved by Fritzing 0.8.7b)
breadboards: 1

parts:
  Part1 = Arduino Uno (Rev3)
  J1 = Basic Servo
  Part3 = Thumb Joystick

nets:
  N1: Part1.A5/SCL, Part3.VERT
  N2: Part1.D9_PWM, J1.pulse
  VCC: Part1.5V, J1.vcc, Part3.VCC
  GND: Part1.GND, J1.gnd, Part3.GND
