# Fritzing sketch shift_register (saved by Fritzing 0.8.7b)
breadboards: 1

parts:
  Part1 = Arduino Uno (Rev3)
  U2 = 74HC595 [package="DIP16 [THT]"]
  LED7 = LED - 5mm [color="Yellow (585nm)" package="5 mm [THT]"]
  LED8 = LED - 5mm [color="Yellow (585nm)" package="5 mm [THT]"]
  LED9 = LED - 5mm [color="Green (560nm)" package="5 mm [THT]"]
  LED10 = LED - 5mm [color="Green (560nm)" package="5 mm [THT]"]
  LED11 = LED - 5mm [color="Red (633nm)" package="5 mm [THT]"]
  LED = LED - 5mm [color="Red (633nm)" package="5 mm [THT]"]
  R1 = Resistor [tolerance=±5% resistance=220 package=THT]
  R2 = Resistor [tolerance=±5% resistance=220 package=THT]
  R3 = Resistor [tolerance=±5% resistance=220 package=THT]
  R4 = Resistor [tolerance=±5% resistance=220 package=THT]
  R5 = Resistor [tolerance=±5% resistance=220 package=THT]
  R6 = Resistor [tolerance=±5% resistance=220 package=THT]
  LED14 = LED - 5mm [color="Red (633nm)" package="5 mm [THT]"]
  R8 = Resistor [tolerance=±5% resistance=220 package=THT]
  R9 = Resistor [tolerance=±5% resistance=220 package=THT]
  LED15 = LED - 5mm [color="Red (635nm)" package="5 mm [THT]"]

nets:
  N1: Part1.D8, U2.ST_CP
  N2: Part1.D11_PWM/MOSI, U2.DS
  N3: Part1.D12/MISO, U2.SH_CP
  5V: Part1.5V, U2.MR, U2.VCC
  GND: Part1.GND, U2.GND, U2.OE, LED7.cathode, LED8.cathode, LED9.cathode, LED10.cathode, LED11.cathode, LED.cathode, LED14.cathode, LED15.cathode
  N4: U2.Q1, R3.Pin_0
  N5: U2.Q2, R4.Pin_0
  N6: U2.Q3, R5.Pin_0
  N7: U2.Q4, R6.Pin_0
  N8: U2.Q5, R1.Pin_0
  N9: U2.Q6, R9.Pin_0
  N10: U2.Q7, R8.Pin_0
  N11: U2.Q0, R2.Pin_0
  N12: LED7.anode, R2.Pin_1
  N13: LED8.anode, R3.Pin_1
  N14: LED9.anode, R4.Pin_1
  N15: LED10.anode, R5.Pin_1
  N16: LED11.anode, R6.Pin_1
  N17: LED.anode, R1.Pin_1
  N18: LED14.anode, R8.Pin_1
  N19: R9.Pin_1, LED15.anode

notes:
  http://arduino.cc/en/tutorial/ShiftOut
