# Fritzing sketch soil_sensor (saved by Fritzing 0.8.7b)
breadboards: 1

parts:
  Part1 = Arduino Uno (Rev3)
  R2 = Resistor [tolerance=±5% resistance=10k package=THT]
  U1 = mystery part, 2 pins [chip_label=?]

nets:
  N1: Part1.A0, R2.Pin_0, U1.pin1
  N2: Part1.5V, U1.pin2
  N3: Part1.GND, R2.Pin_1
