# Fritzing sketch solar_charging (saved by Fritzing 0.8.7b)
breadboards: 1

parts:
  Diode = Rectifier Diode [part_number=1N4001 package="300 mil [THT]"]
  Rechargable_batteries = 4 x AAA Battery Mount
  Solar_panel_5_5V_at_170mA = SOLAR-IXYS [package=solarbit-12x1]

nets:
  N1: Diode.cathode, Rechargable_batteries.+
  N2: Diode.anode, Solar_panel_5_5V_at_170mA.A
  N3: Rechargable_batteries.-, Solar_panel_5_5V_at_170mA.C

notes:
  RECHARGABLE BATTERIES
