# Fritzing sketch thumbstick (saved by Fritzing 0.8.7b)
breadboards: 1

parts:
  Part1 = Arduino Uno (Rev3)
  LED1 = LED - 5mm [color="Red (633nm)" package="5 mm [THT]"]
  R3 = Resistor [tolerance=±5% resistance=220 package=THT]
  Part2 = Thumb Joystick
  R4 = Resistor [tolerance=±5% resistance=220 package=THT]
  LED2 = LED - 5mm [color="Red (633nm)" package="5 mm [THT]"]

nets:
  N1: Part1.A4/SDA, Part2.HORZ
  N2: Part1.A5/SCL, Part2.VERT
  N3: Part1.D10_PWM/SS, R4.Pin_0
  N4: Part1.D11_PWM/MOSI, R3.Pin_0
  GND: Part1.GND, LED1.cathode, Part2.GND, LED2.cathode
  5V: Part1.5V, Part2.VCC
  N5: LED1.anode, R3.Pin_1
  N6: R4.Pin_1, LED2.anode
