# Fritzing sketch whiskers (saved by Fritzing 0.8.7b)

parts:
  Part1 = Arduino Uno (Rev3)
  Part2 = Thumb Joystick

nets:
  N1: Part1.A4/SDA, Part2.SEL, Part2.HORZ
  N2: Part1.A5/SCL, Part2.VERT
  5V: Part1.5V, Part2.VCC
  GND: Part1.GND, Part2.GND
