# Fritzing sketch magbot (saved by Fritzing 0.8.7b)
breadboards: 1

parts:
  Motor_Shield = Arduino Motor Shield (Rev3)
  Motor_A = DC Motor
  Motor_B = DC Motor
  Ping_Sensor = SRF05 Ultrasonic Rangefinder
  Buzzer = Piezo Speaker
  R1 = Rotary Potentiometer (Small) [maximum_resistance=100kΩ package=THT]  # not connected
  S1 = Pushbutton [package="[THT]"]  # not connected
  R2 = Resistor [tolerance=±5% resistance=220 package=THT]
  VCC1 = 4 x AAA Battery Mount

nets:
  GND: Motor_Shield.GND, Ping_Sensor.GND, Buzzer.pin1, VCC1.-
  N1: Motor_Shield.D2, R2.Pin_1
  N2: Motor_Shield.D4, Ping_Sensor.Echo
  N3: Motor_Shield.D7, Ping_Sensor.Trig
  N4: Motor_Shield.B-, Motor_A.pin_2
  N5: Motor_Shield.B+, Motor_A.pin_1
  N6: Motor_Shield.A-, Motor_B.pin_2
  N7: Motor_Shield.A+, Motor_B.pin_1
  N8: Motor_Shield.VMOT, VCC1.+
  5V: Motor_Shield.5V, Ping_Sensor.VCC
  N9: Buzzer.pin2, R2.Pin_0
